// Logisim project Lab3.circ as structural Verilog: 8 circuits, main circuit main
module main (
  input  I30,
  input  I14,
  input  I13,
  input  I12,
  input  I6,
  input  I5,
  input  I4,
  output ALU_Ctrl3,
  output ALU_Ctrl2,
  output ALU_Ctrl1,
  output ALU_Ctrl0,
  output ALU_Src
);

  wire and_2_out, not_1_out, not_2_out, not_3_out, not_4_out, not_5_out;

  not not_1 (not_1_out, I14);
  not not_2 (not_2_out, I13);
  not not_3 (not_3_out, I12);
  not not_4 (not_4_out, I5);
  not not_5 (not_5_out, I4);
  and and_1 (ALU_Ctrl2, I30, not_2_out, I5);
  or or_1 (ALU_Ctrl1, not_2_out, not_5_out);
  and and_2 (and_2_out, I13, not_3_out);
  or or_2 (ALU_Src, not_4_out, not_5_out);
  or or_3 (ALU_Ctrl0, not_1_out, and_2_out);

  assign ALU_Ctrl3 = 1'b0;
endmodule

module full_adder (
  input  A,
  input  B,
  input  C_in,
  output S,
  output C_out
);

  wire and_1_out, and_2_out, xor_1_out;

  xor xor_1 (xor_1_out, A, B);
  and and_1 (and_1_out, xor_1_out, C_in);
  and and_2 (and_2_out, A, B);
  xor xor_2 (S, xor_1_out, C_in);
  or or_1 (C_out, and_1_out, and_2_out);
endmodule

module one_bit_ALU (
  input  [3:0] ALU_Ctrl,
  input  A,
  input  B,
  input  C_in,
  output R,
  output C_out
);

  wire and_1_out, full_adder_1_s, multiplexer_1_out, not_1_out, or_1_out, xor_1_out;

  Multiplexer #(.enable("false")) multiplexer_1 (.in0(B), .in1(not_1_out), .out(multiplexer_1_out), .sel(ALU_Ctrl[2]));
  not not_1 (not_1_out, B);
  and and_1 (and_1_out, A, multiplexer_1_out);
  or or_1 (or_1_out, A, multiplexer_1_out);
  xor xor_1 (xor_1_out, A, multiplexer_1_out);
  Multiplexer #(.enable("false"), .select(2)) multiplexer_2 (
    .in0(and_1_out), .in1(or_1_out), .in2(xor_1_out), .in3(full_adder_1_s), .out(R), .sel(ALU_Ctrl[1:0]));
  full_adder full_adder_1 (.A(A), .B(multiplexer_1_out), .C_in(C_in), .S(full_adder_1_s), .C_out(C_out));
endmodule

module four_bit_ALU (
  input  [3:0] ALU_Ctrl,
  input  [3:0] A,
  input  [3:0] B,
  input  C_in,
  output [3:0] R,
  output C_out
);

  wire one_bit_alu_1_c_out, one_bit_alu_2_c_out, one_bit_alu_3_c_out;

  one_bit_ALU one_bit_alu_1 (
    .ALU_Ctrl(ALU_Ctrl), .A(A[0]), .B(B[0]), .C_in(C_in), .R(R[0]), .C_out(one_bit_alu_1_c_out));
  one_bit_ALU one_bit_alu_2 (
    .ALU_Ctrl(ALU_Ctrl), .A(A[1]), .B(B[1]), .C_in(one_bit_alu_1_c_out), .R(R[1]), .C_out(one_bit_alu_2_c_out));
  one_bit_ALU one_bit_alu_3 (
    .ALU_Ctrl(ALU_Ctrl), .A(A[2]), .B(B[2]), .C_in(one_bit_alu_2_c_out), .R(R[2]), .C_out(one_bit_alu_3_c_out));
  one_bit_ALU one_bit_alu_4 (
    .ALU_Ctrl(ALU_Ctrl), .A(A[3]), .B(B[3]), .C_in(one_bit_alu_3_c_out), .R(R[3]), .C_out(C_out));
endmodule

module ALU32 (
  input  [3:0] ALU_Ctrl,
  input  [31:0] A,
  input  [31:0] B,
  output [31:0] R,
  output C_out
);

  wire four_bit_alu_1_c_out, four_bit_alu_2_c_out, four_bit_alu_3_c_out, four_bit_alu_4_c_out,
       four_bit_alu_5_c_out, four_bit_alu_6_c_out, four_bit_alu_7_c_out;
  wire [3:3] undriven;

  four_bit_ALU four_bit_alu_1 (
    .ALU_Ctrl({undriven[3], ALU_Ctrl[2:0]}), .A(A[3:0]), .B(B[3:0]), .C_in(ALU_Ctrl[2]), .R(R[3:0]),
    .C_out(four_bit_alu_1_c_out));
  four_bit_ALU four_bit_alu_2 (
    .ALU_Ctrl({undriven[3], ALU_Ctrl[2:0]}), .A(A[7:4]), .B(B[7:4]), .C_in(four_bit_alu_1_c_out), .R(R[7:4]),
    .C_out(four_bit_alu_2_c_out));
  four_bit_ALU four_bit_alu_3 (
    .ALU_Ctrl({undriven[3], ALU_Ctrl[2:0]}), .A(A[11:8]), .B(B[11:8]), .C_in(four_bit_alu_2_c_out),
    .R(R[11:8]), .C_out(four_bit_alu_3_c_out));
  four_bit_ALU four_bit_alu_4 (
    .ALU_Ctrl({undriven[3], ALU_Ctrl[2:0]}), .A(A[15:12]), .B(B[15:12]), .C_in(four_bit_alu_3_c_out),
    .R(R[15:12]), .C_out(four_bit_alu_4_c_out));
  four_bit_ALU four_bit_alu_5 (
    .ALU_Ctrl({undriven[3], ALU_Ctrl[2:0]}), .A(A[19:16]), .B(B[19:16]), .C_in(four_bit_alu_4_c_out),
    .R(R[19:16]), .C_out(four_bit_alu_5_c_out));
  four_bit_ALU four_bit_alu_6 (
    .ALU_Ctrl({undriven[3], ALU_Ctrl[2:0]}), .A(A[23:20]), .B(B[23:20]), .C_in(four_bit_alu_5_c_out),
    .R(R[23:20]), .C_out(four_bit_alu_6_c_out));
  four_bit_ALU four_bit_alu_7 (
    .ALU_Ctrl({undriven[3], ALU_Ctrl[2:0]}), .A(A[27:24]), .B(B[27:24]), .C_in(four_bit_alu_6_c_out),
    .R(R[27:24]), .C_out(four_bit_alu_7_c_out));
  four_bit_ALU four_bit_alu_8 (
    .ALU_Ctrl({undriven[3], ALU_Ctrl[2:0]}), .A(A[31:28]), .C_in(four_bit_alu_7_c_out), .R(R[31:28]),
    .C_out(C_out));  // open: B
endmodule

module Register32 (
  input  [1:0] RReg1,
  input  [1:0] RReg2,
  input  [31:0] WData,
  input  Clock_in,
  input  Write,
  input  [1:0] WReg,
  output [31:0] RData1,
  output [31:0] RData2
);

  wire demultiplexer_1_out0, demultiplexer_1_out1, demultiplexer_1_out2, demultiplexer_1_out3;
  wire [31:0] register_1_q, register_2_q, register_3_q, register_4_q;

  Demultiplexer #(.enable("false"), .select(2)) demultiplexer_1 (
    .out0(demultiplexer_1_out0), .out1(demultiplexer_1_out1), .out2(demultiplexer_1_out2),
    .out3(demultiplexer_1_out3), .in(Write), .sel(WReg));
  Register #(.width(32)) register_1 (
    .D(WData), .en(demultiplexer_1_out0), .clk(Clock_in), .Q(register_1_q), .clr(Write));
  Register #(.width(32)) register_2 (
    .D(WData), .en(demultiplexer_1_out1), .clk(Clock_in), .Q(register_2_q));  // open: clr
  Register #(.width(32)) register_3 (
    .D(WData), .en(demultiplexer_1_out2), .clk(Clock_in), .Q(register_3_q));  // open: clr
  Register #(.width(32)) register_4 (
    .D(WData), .en(demultiplexer_1_out3), .clk(Clock_in), .Q(register_4_q));  // open: clr
  Multiplexer #(.enable("false"), .select(2), .width(32)) multiplexer_1 (
    .in0(register_1_q), .in1(register_2_q), .in2(register_3_q), .in3(register_4_q), .out(RData1), .sel(RReg1));
  Multiplexer #(.enable("false"), .select(2), .width(32)) multiplexer_2 (
    .in0(register_1_q), .in1(register_2_q), .in2(register_3_q), .in3(register_4_q), .out(RData2), .sel(RReg2));
endmodule

module Register32_32 (
  input  Clock_in,
  input  [4:0] RReg1,
  input  [4:0] RReg2,
  input  [31:0] WData,
  input  Write,
  input  [4:0] WReg,
  output [31:0] RData1,
  output [31:0] RData2
);

  wire W3_0, W7_4, W11_8, W15_12, W19_16, W23_20, W27_24, W31_28;
  wire [31:0] register32_1_rdata1, register32_1_rdata2, register32_2_rdata1, register32_2_rdata2,
       register32_3_rdata1, register32_3_rdata2, register32_4_rdata1, register32_4_rdata2,
       register32_5_rdata1, register32_5_rdata2, register32_6_rdata1, register32_6_rdata2,
       register32_7_rdata1, register32_7_rdata2, register32_8_rdata1, register32_8_rdata2;

  Demultiplexer #(.enable("false"), .select(3)) demultiplexer_1 (
    .out0(W3_0), .out1(W7_4), .out2(W11_8), .out3(W15_12), .out4(W19_16), .out5(W23_20), .out6(W27_24),
    .out7(W31_28), .in(Write), .sel(WReg[4:2]));
  Register32 register32_1 (
    .RReg1(RReg1[1:0]), .RReg2(RReg2[1:0]), .WData(WData), .Clock_in(Clock_in), .Write(W3_0),
    .WReg(WReg[1:0]), .RData1(register32_1_rdata1), .RData2(register32_1_rdata2));
  Register32 register32_2 (
    .RReg1(RReg1[1:0]), .RReg2(RReg2[1:0]), .WData(WData), .Clock_in(Clock_in), .Write(W7_4),
    .WReg(WReg[1:0]), .RData1(register32_2_rdata1), .RData2(register32_2_rdata2));
  Register32 register32_3 (
    .RReg1(RReg1[1:0]), .RReg2(RReg2[1:0]), .WData(WData), .Clock_in(Clock_in), .Write(W11_8),
    .WReg(WReg[1:0]), .RData1(register32_3_rdata1), .RData2(register32_3_rdata2));
  Register32 register32_4 (
    .RReg1(RReg1[1:0]), .RReg2(RReg2[1:0]), .WData(WData), .Clock_in(Clock_in), .Write(W15_12),
    .WReg(WReg[1:0]), .RData1(register32_4_rdata1), .RData2(register32_4_rdata2));
  Register32 register32_5 (
    .RReg1(RReg1[1:0]), .RReg2(RReg2[1:0]), .WData(WData), .Clock_in(Clock_in), .Write(W19_16),
    .WReg(WReg[1:0]), .RData1(register32_5_rdata1), .RData2(register32_5_rdata2));
  Register32 register32_6 (
    .RReg1(RReg1[1:0]), .RReg2(RReg2[1:0]), .WData(WData), .Clock_in(Clock_in), .Write(W23_20),
    .WReg(WReg[1:0]), .RData1(register32_6_rdata1), .RData2(register32_6_rdata2));
  Register32 register32_7 (
    .RReg1(RReg1[1:0]), .RReg2(RReg2[1:0]), .WData(WData), .Clock_in(Clock_in), .Write(W27_24),
    .WReg(WReg[1:0]), .RData1(register32_7_rdata1), .RData2(register32_7_rdata2));
  Register32 register32_8 (
    .RReg1(RReg1[1:0]), .RReg2(RReg2[1:0]), .WData(WData), .Clock_in(Clock_in), .Write(W31_28),
    .WReg(WReg[1:0]), .RData1(register32_8_rdata1), .RData2(register32_8_rdata2));
  Multiplexer #(.enable("false"), .select(3), .width(32)) multiplexer_1 (
    .in0(register32_1_rdata1), .in1(register32_2_rdata1), .in2(register32_3_rdata1),
    .in3(register32_4_rdata1), .in4(register32_5_rdata1), .in5(register32_6_rdata1),
    .in6(register32_7_rdata1), .in7(register32_8_rdata1), .out(RData1), .sel(RReg1[4:2]));
  Multiplexer #(.enable("false"), .select(3), .width(32)) multiplexer_2 (
    .in0(register32_1_rdata2), .in1(register32_2_rdata2), .in2(register32_3_rdata2),
    .in3(register32_4_rdata2), .in4(register32_5_rdata2), .in5(register32_6_rdata2),
    .in6(register32_7_rdata2), .in7(register32_8_rdata2), .out(RData2), .sel(RReg2[4:2]));
endmodule

module Datapath (
  input  [31:0] Instruction
);

  wire clock_1_out, main_1_alu_src;
  wire [3:0] main_1_alu_ctrl0;
  wire [31:0] alu32_1_r, bit_extender_1_out, multiplexer_1_out, register32_32_1_rdata1,
       register32_32_1_rdata2;

  Clock clock_1 (.out(clock_1_out));
  assign bit_extender_1_out = {{20{Instruction[31]}}, Instruction[31:20]};  // Bit_Extender bit_extender_1
  Register32_32 register32_32_1 (
    .Clock_in(clock_1_out), .RReg1(Instruction[19:15]), .RReg2(Instruction[24:20]), .WData(alu32_1_r),
    .Write(1'b1), .WReg(Instruction[11:7]), .RData1(register32_32_1_rdata1), .RData2(register32_32_1_rdata2));
  Multiplexer #(.enable("false"), .width(32)) multiplexer_1 (
    .in0(register32_32_1_rdata2), .in1(bit_extender_1_out), .out(multiplexer_1_out), .sel(main_1_alu_src));
  main main_1 (
    .I30(Instruction[30]), .I14(Instruction[14]), .I13(Instruction[13]), .I12(Instruction[12]),
    .I6(Instruction[6]), .I5(Instruction[5]), .I4(Instruction[4]), .ALU_Ctrl3(main_1_alu_ctrl0[3]),
    .ALU_Ctrl2(main_1_alu_ctrl0[2]), .ALU_Ctrl1(main_1_alu_ctrl0[1]), .ALU_Ctrl0(main_1_alu_ctrl0[0]),
    .ALU_Src(main_1_alu_src));
  ALU32 alu32_1 (
    .ALU_Ctrl(main_1_alu_ctrl0), .A(register32_32_1_rdata1), .B(multiplexer_1_out), .R(alu32_1_r));  // open: C_out
endmodule
